# Fritzing sketch Untitled Sketch 2 (saved by Fritzing 0.9.3b)
breadboards: 1

parts:
  Parte1 = Arduino Uno (Rev3)
  Parte2 = Bluetooth HC-05 Macho
  Parte3 = Breakout Board for Electret Microphone

nets:
  N1: Parte1.A0, Parte3.VCC
  N2: Parte1.D0/RX, Parte2.TXD
  N3: Parte1.D1/TX, Parte2.RXD
  5V: Parte1.5V, Parte2.VCC, Parte3.AUD
  GND: Parte1.GND, Parte2.GND, Parte3.GND
